# Fritzing sketch LED Switch (saved by Fritzing 0.9.2b)
breadboards: 1

parts:
  Raspberry_Pi1 = Raspberry Pi 2
  S1 = Pushbutton [package="[THT]"]
  R1 = Resistor [tolerance=±5% resistance=10k package=THT]
  LED1 = LED - 5mm [color="Red (633nm)" package="5 mm [THT]"]
  R2 = Resistor [tolerance=±5% resistance=330 package=THT]

nets:
  N1: Raspberry_Pi1.3v3, S1.Pin_3, S1.Pin_4
  N2: Raspberry_Pi1.GPIO5, S1.Pin_1, S1.Pin_2, R1.Pin_0
  N3: Raspberry_Pi1.GPIO6, R2.Pin_1
  N4: Raspberry_Pi1.GND, R1.Pin_1, LED1.cathode
  N5: LED1.anode, R2.Pin_0

notes:
  GPIO5 タクトスイッチ
  GPIO6 LED
